# Fritzing sketch troolebot (saved by Fritzing 0.8.7b)
breadboards: 3

parts:
  LED1 = LED - 5mm [color="Red (633nm)" package="5 mm [THT]"]
  C1 = Electrolytic Capacitor [capacitance=10µF voltage=35V package="100 mil [THT, electrolytic]"]
  J1 = Basic Servo
  J2 = Infrared Proximity Sensor [part_number=2y0a21]
  J3 = Piezo Speaker
  Parte1 = Arduino Uno (Rev3)
  Parte2 = Arduino XBee Shield
  IC1 = IC, DIP package, 16 pins [chip_label=IC part_number=4511]
  R1 = Resistor [tolerance=±5% resistance=300 package=THT]
  7_Segment1 = 7 Segment Display
  C2 = Ceramic Capacitor [capacitance=100nF voltage=35V package="100 mil [THT, multilayer]"]
  S1 = Pushbutton [package="[THT]"]
  R2 = Resistor [tolerance=±5% resistance=4.7k package=THT]
  R3 = Resistor [tolerance=±5% resistance=300 package=THT]
  R4 = Resistor [tolerance=±5% resistance=300 package=THT]
  R5 = Resistor [tolerance=±5% resistance=300 package=THT]
  R6 = Resistor [tolerance=±5% resistance=300 package=THT]
  R7 = Resistor [tolerance=±5% resistance=300 package=THT]
  R8 = Resistor [tolerance=±5% resistance=300 package=THT]
  R9 = Resistor [tolerance=±5% resistance=300 package=THT]
  R10 = Resistor [tolerance=±5% resistance=4.7k package=THT]
  R11 = Resistor [tolerance=±5% resistance=4.7k package=THT]
  Q3 = NPN-Transistor [part_number=bc547 package="TO92 [THT]"]
  D1 = Rectifier Diode [part_number=1N4148 package="300 mil [THT]"]
  LED2 = LED - 5mm [color="White (6500K)" package="5 mm [THT]"]
  LED3 = LED - 5mm [color="Red (633nm)" package="5 mm [THT]"]
  LED4 = LED - 5mm [color="White (6500K)" package="5 mm [THT]"]
  R12 = Resistor [tolerance=±5% resistance=220 package=THT]
  R13 = Resistor [tolerance=±5% resistance=220 package=THT]
  R14 = Resistor [tolerance=±5% resistance=220 package=THT]
  R15 = Resistor [tolerance=±5% resistance=220 package=THT]
  Q5 = QRD1114 [part_number=cny70 package=qrd1114]
  Q6 = QRD1114 [part_number=cny70 package=qrd1114]
  R16 = Resistor [tolerance=±5% resistance=10k package=THT]
  R17 = Resistor [tolerance=±5% resistance=150 package=THT]
  R18 = Resistor [tolerance=±5% resistance=150 package=THT]
  R19 = Resistor [tolerance=±5% resistance=10k package=THT]
  C3 = Ceramic Capacitor [capacitance=330nF voltage=35V package="100 mil [THT, multilayer]"]
  R20 = Resistor [tolerance=±5% resistance=330 package=THT]
  R21 = Resistor [tolerance=±5% resistance=220 package=THT]
  U1 = Voltage Regulator - Variable [package="TO220 [THT]"]
  C5 = Ceramic Capacitor [capacitance=100nF voltage=35V package="100 mil [THT, multilayer]"]
  R22 = Resistor [tolerance=±5% resistance=4.7k package=THT]
  R23 = Resistor [tolerance=±5% resistance=4.7k package=THT]
  R24 = Resistor [tolerance=±5% resistance=1k package=THT]
  R25 = Resistor [tolerance=±5% resistance=1k package=THT]
  Q7 = PNP-Transistor [part_number=bc557 package="TO92 [THT]"]
  Q8 = PNP-Transistor [part_number=bc557 package="TO92 [THT]"]
  Q9 = NPN-Transistor [part_number=bc547 package="TO92 [THT]"]
  R26 = Resistor [tolerance=±5% resistance=4.7k package=THT]
  D2 = Rectifier Diode [part_number=1N4148 package="300 mil [THT]"]
  R27 = Resistor [tolerance=±5% resistance=220 package=THT]
  LED5 = LED - 3mm [color="Red (633nm)" package="3 mm [THT]"]
  C6 = Electrolytic Capacitor [capacitance=10µF voltage=35V package="100 mil [THT, electrolytic]"]
  D3 = Rectifier Diode [part_number=1N4148 package="300 mil [THT]"]
  C7 = Ceramic Capacitor [capacitance=100nF voltage=35V package="100 mil [THT, multilayer]"]
  C8 = Ceramic Capacitor [capacitance=100nF voltage=35V package="100 mil [THT, multilayer]"]
  M1 = DC Motor
  M2 = DC Motor
  U2 = RELAY-2 [package=relay-g5v]
  U3 = RELAY-2 [package=relay-g5v]
  Q4 = NPN-Transistor [part_number=bc547 package="TO92 [THT]"]
  Q10 = npn-Powertransistor [part_number=bd137 package="TO220 [THT]"]
  Q11 = npn-Powertransistor [part_number=bd137 package="TO220 [THT]"]

nets:
  N1: LED1.cathode, R12.Pin_0
  VCC: LED1.anode, J1.vcc, J2.Vcc, J3.pin2, Parte1.5V, Parte2.5V, IC1.pin3, IC1.pin4, IC1.pin16, C2.0, S1.Pin_1, S1.Pin_2, D1.cathode, LED2.anode, LED3.anode, LED4.anode, R16.Pin_1, R17.Pin_1, R18.Pin_1, R19.Pin_1, Q7.E, Q8.E
  GND: C1.-, J1.gnd, J2.GND, Parte2.GND, IC1.pin5, IC1.pin8, 7_Segment1.common_cathode, C2.1, R10.Pin_0, Q3.E, Q5.E, Q5.K, Q6.E, Q6.K, C3.0, R20.Pin_0, C5.0, Q9.E, Q4.E, Q10.emitter, Q11.emitter
  VIN: C1.+, Parte1.VIN, Parte2.VIN, U1.IN, C5.1, D2.cathode, U2.9, U3.9
  N2: J1.pulse, Parte1.D9_PWM, Parte2.D9
  N3: J2.Vout, Parte1.A0, Parte2.A0
  N4: J3.pin1, D1.anode, Q4.C
  N5: Parte1.A1, Parte2.A1, IC1.pin7
  N6: Parte1.A2, Parte2.A2, IC1.pin1
  N7: Parte1.A3, Parte2.A3, IC1.pin2
  N8: Parte1.A4/SDA, Parte2.A4, IC1.pin6
  N9: Parte1.A5/SCL, Parte2.A5, R6.Pin_0
  N10: Parte1.D8, Parte2.D8
  N11: Parte1.D10_PWM/SS, Parte2.D10, R22.Pin_1, R23.Pin_1
  N12: Parte1.D11_PWM/MOSI, Parte2.D11
  N13: Parte1.D12/MISO, Parte2.D12
  N14: Parte1.D13/SCK, Parte2.D13
  N15: Parte1.AREF, Parte2.AREF
  N16: Parte1.D0/RX, Parte2.UART_RX
  N17: Parte1.D1/TX, Parte2.UART_TX
  N18: Parte1.D2, Parte2.D_RX, R11.Pin_1
  N19: Parte1.D3_PWM, Parte2.D_TX, R2.Pin_1
  N20: Parte1.D4, Parte2.D4, R26.Pin_1
  N21: Parte1.D5_PWM, Parte2.D5, Q5.C, R19.Pin_0
  N22: Parte1.D6_PWM, Parte2.D6, Q6.C, R16.Pin_0
  N23: Parte1.D7, Parte2.D7, S1.Pin_3, S1.Pin_4, R10.Pin_1
  N24: Parte1.RESET, Parte2.RST
  N25: Parte1.GND, Parte2.N$138
  N26: IC1.pin9, R1.Pin_0
  N27: IC1.pin10, R8.Pin_0
  N28: IC1.pin11, R5.Pin_0
  N29: IC1.pin12, R4.Pin_0
  N30: IC1.pin13, R7.Pin_0
  N31: IC1.pin14, R9.Pin_0
  N32: IC1.pin15, R3.Pin_0
  N33: R1.Pin_1, 7_Segment1.Segment_E
  N34: 7_Segment1.Segment_A#1, R9.Pin_1
  N35: 7_Segment1.Segment_F, R3.Pin_1
  N36: 7_Segment1.Segment_D, R8.Pin_1
  N37: 7_Segment1.Segment_DP, R6.Pin_1
  N38: 7_Segment1.Segment_C, R5.Pin_1
  N39: 7_Segment1.Segment_B, R4.Pin_1
  N40: 7_Segment1.Segment_A#10, R7.Pin_1
  N41: R2.Pin_0, Q4.B
  N42: R11.Pin_0, Q3.B
  N43: Q3.C, R12.Pin_1, R13.Pin_1, R14.Pin_1, R15.Pin_1
  N44: LED2.cathode, R14.Pin_0
  N45: LED3.cathode, R13.Pin_0
  N46: LED4.cathode, R15.Pin_0
  N47: Q5.A, R18.Pin_0
  N48: Q6.A, R17.Pin_0
  N49: C3.1, R21.Pin_0, U1.OUT, LED5.anode, C6.+, D3.cathode, U2.10, U3.1
  N50: R20.Pin_1, R21.Pin_1, U1.ADJ
  N51: R22.Pin_0, Q7.B
  N52: R23.Pin_0, Q8.B
  N53: R24.Pin_0, Q7.C
  N54: R24.Pin_1, Q10.base
  N55: R25.Pin_0, Q8.C
  N56: R25.Pin_1, Q11.base
  N57: Q9.B, R26.Pin_0
  N58: Q9.C, D2.anode, U2.2, U3.2
  N59: R27.Pin_0, LED5.cathode
  N60: R27.Pin_1, C6.-, D3.anode, U2.1, U3.10, Q10.collector, Q11.collector
  N61: C7.0, C8.0, M1.pin_2, M2.pin_2, U2.5
  N62: C7.1, C8.1, M1.pin_1, M2.pin_1, U3.5
